# Fritzing sketch AQ_Board (saved by Fritzing 0.8.7b)
circuit board: 4.92451cm x 4.02846cm
breadboards: 1

parts:
  part = Resistor [tolerance=±5% resistance=220 package=THT]
  part_2 = female pin header, 3 pins [form="♀ (female)"]
  part_3 = female pin header, 3 pins [form="♀ (female)"]
  part_4 = female pin header, 3 pins [form="♀ (female)"]
  part_5 = female pin header, 6 pins [form="♀ (female)"]
  part_6 = female pin header, 4 pins [form="♀ (female)"]

nets:
  N1: part.Pin_0, part_2.pin2, part_3.pin2, part_4.pin2
  N2: part.Pin_1, part_2.pin1, part_3.pin1, part_4.pin3, part_5.pin1
  N3: part_2.pin3, part_3.pin3, part_4.pin1
  N4: part_5.pin2, part_6.pin4
  N5: part_5.pin3, part_6.pin3
  N6: part_5.pin4, part_6.pin2
  N7: part_5.pin5, part_6.pin1

notes:
  5v - Relays
  Power + Data
  4.7k Ohm
  DS18B20_1
  DS18B20_2
  Relays
